// Logisim project 2_decoder_sm.circ as structural Verilog: 1 circuit, main circuit main
module main (
  input  R,
  input  Q,
  input  P,
  output A,
  output B,
  output C,
  output D,
  output E,
  output F,
  output G
);

  not not_1 (A, R);
  not not_2 (C, Q);
  not not_3 (B, P);
  and and_1 (F, B, C, A);

  assign D = A;
  assign E = A;
  assign G = Q;
endmodule
